# Fritzing sketch dc_wiring (saved by Fritzing 0.9.5d)
breadboards: 1

parts:
  XIAO_nRF52840_Plus1 = prefix0000FUISUIvvv [chip_label="XIAO nRF52840  Plus"]
  U1 = LIPO-1000mAh [part_number=500mah package=lipo-1000]
  U2 = Pololu U1V11F5 [package=THT]
  Dreamcast_Controller_In = Hirose DF13 Series Header [part_number=DF13#-5P-1.25V package=DF13C-5P-1.25V]
  R1 = Resistor [tolerance=±5% resistance=10k package="1206 [SMD]"]
  R2 = Resistor [tolerance=±5% resistance=10k package="1206 [SMD]"]
  D1 = Schottky Diode [part_number=1N5817 package="300 mil [THT]"]
  D2 = Schottky Diode [part_number=1N5817 package="300 mil [THT]"]
  S1 = Momentary Switch [package=tactile-pth]

nets:
  N1: XIAO_nRF52840_Plus1.connector2, U2.SHDN
  N2: XIAO_nRF52840_Plus1.connector4, Dreamcast_Controller_In.5, R1.Pin_0
  N3: XIAO_nRF52840_Plus1.connector5, Dreamcast_Controller_In.1, R2.Pin_0
  N4: XIAO_nRF52840_Plus1.connector10, S1.1
  N5: XIAO_nRF52840_Plus1.connector11, R1.Pin_1, R2.Pin_1
  N6: XIAO_nRF52840_Plus1.connector12, U1.-, U2.GND, Dreamcast_Controller_In.3, Dreamcast_Controller_In.4, S1.2
  N7: XIAO_nRF52840_Plus1.connector13, D2.anode
  N8: U1.+, U2.VIN
  N9: U2.VOUT, D1.anode
  N10: Dreamcast_Controller_In.2, D1.cathode, D2.cathode

notes:
  Battery soldered to BAT+/BAT- pads on underside of XIAO.

custom parts:
  Pololu U1V11F5: Mini-360 DC-DC Buck converter. Tiny buck step down voltage converter, input voltage 4.75 to 23V output 1 to 17V adjustable. Available from ebay and the like.
